# Fritzing sketch ECU-Bombyx (saved by Fritzing 0.9.4)
circuit board: 8.46667cm x 5.64444cm
breadboards: 1

parts:
  microSD1 = MicroSD Card Module
  PCB3 = RTC_DS1302_module
  Componente3 = Adafruit SGP30 Gas Sensor
  Componente2 = Arduino Uno (Rev3)
  DHT1 = DHT22 module

nets:
  GND: microSD1.GND, PCB3.GND, Componente3.GND, Componente2.GND, DHT1.GND
  VCC: microSD1.VCC, PCB3.VCC, Componente3.VIN, Componente2.5V, DHT1.VCC
  N1: microSD1.MISO, Componente2.D12/MISO
  N2: microSD1.MOSI, Componente2.D11_PWM/MOSI
  N3: microSD1.SCK, Componente2.D13/SCK
  N4: microSD1.CS, Componente2.D8
  N5: PCB3.RST, Componente2.A0
  N6: PCB3.DAT, Componente2.A1
  N7: PCB3.CLK, Componente2.A2
  N8: Componente3.SCL, Componente2.A5/SCL
  N9: Componente3.SDA, Componente2.A4/SDA
  N10: Componente2.D2, DHT1.DAT

custom parts:
  RTC_DS1302_module: Arduino module DS1302 SPI Real Time Clock
  DHT22 module: Digital relative humidity & temperature sensor DHT22 module
